// Logisim project main.circ as structural Verilog
module ram (
  input  [15:0] Address,
  input  [15:0] Data_in,
  input  Clear,
  input  Chip_Select,
  input  Read__0____write__1,
  output [15:0] Data_out
);

  wire and_1_out, not_1_out, not_2_out;
  wire [15:0] ram_1_data;

  not not_1 (not_1_out, Read__0____write__1);
  RAM #(.addrWidth(16), .dataWidth(16), .bus("separate")) ram_1 (
    .addr(Address), .din(Data_in), .data(ram_1_data), .str(Read__0____write__1), .sel(Chip_Select),
    .clk(not_2_out), .ld(not_1_out), .clr(Clear));
  not not_2 (not_2_out, Chip_Select);
  and and_1 (and_1_out, Chip_Select, not_1_out);
  assign Data_out = and_1_out ? ram_1_data : 16'bz;  // Controlled_Buffer controlled_buffer_1

  // Notes on the sheet:
  //   128KB RAM module
endmodule

module alu (
  input  [15:0] Input_A,
  input  [15:0] Input_B,
  input  nB,
  input  [2:0] Op_code,
  output [15:0] Output,
  output [3:0] V_C_Z_S
);

  wire xnor_1_out, xor_2_out;
  wire [15:0] adder_1_out, and_1_out, B, not_1_out, not_2_out, or_1_out, shifter_1_out, shifter_2_out,
       shifter_3_out, xor_1_out;

  Multiplexer #(.width(16), .disabled(0), .enable("false")) multiplexer_1 (
    .in0(Input_B), .in1(not_1_out), .out(B), .sel(nB));
  assign not_1_out = ~Input_B;  // NOT_Gate not_1, 16 bits wide
  Adder #(.width(16)) adder_1 (.a(Input_A), .b(B), .out(adder_1_out), .cin(nB), .cout(V_C_Z_S[2]));
  assign and_1_out = Input_A & B;  // AND_Gate and_1, 16 bits wide
  assign or_1_out = Input_A | B;  // OR_Gate or_1, 16 bits wide
  assign xor_1_out = Input_A ^ B;  // XOR_Gate xor_1, 16 bits wide
  assign not_2_out = ~Input_A;  // NOT_Gate not_2, 16 bits wide
  Shifter #(.width(16)) shifter_1 (.in(Input_A), .\dist (B[3:0]), .out(shifter_1_out));
  Shifter #(.width(16), .shift("lr")) shifter_2 (.in(Input_A), .\dist (B[3:0]), .out(shifter_2_out));
  Shifter #(.width(16), .shift("ar")) shifter_3 (.in(Input_A), .\dist (B[3:0]), .out(shifter_3_out));
  Multiplexer #(.select(3), .width(16), .disabled(0), .enable("false")) multiplexer_2 (
    .in0(adder_1_out), .in1(and_1_out), .in2(or_1_out), .in3(xor_1_out), .in4(not_2_out),
    .in5(shifter_1_out), .in6(shifter_2_out), .in7(shifter_3_out), .out(Output), .sel(Op_code));
  xor xor_2 (xor_2_out, Input_A[15], Output[15]);
  xnor xnor_1 (xnor_1_out, Input_A[15], B[15]);
  and and_2 (V_C_Z_S[3], xnor_1_out, xor_2_out);
  Comparator #(.width(16)) comparator_1 (.a(Output), .b({16{1'b0}}), .eq(V_C_Z_S[1]));  // open: gt, lt

  assign V_C_Z_S[0] = Output[15];

  // Other names for the same wires on the sheet: A[15:0] = Input_A; O[15:0] = Output; c_out = V_C_Z_S[2]

  // Notes on the sheet:
  //   16bit ALU
  //   Flags control
endmodule

module reg_16b (
  input  [15:0] Data,
  input  Input_Enable,
  input  Output_Enable,
  input  Clock,
  input  Clear,
  output [15:0] Output
);

  wire and_1_out;
  wire [15:0] register_1_q;

  Register #(.width(16)) register_1 (.D(Data), .en(and_1_out), .Q(register_1_q), .clk(and_1_out), .clr(Clear));
  and and_1 (and_1_out, Input_Enable, ~Clock);  // AND_Gate
  assign Output = Output_Enable ? register_1_q : 16'bz;  // Controlled_Buffer controlled_buffer_1

  // Notes on the sheet:
  //   General purpose 16bit register
endmodule

module reg_4b (
  input  [3:0] Data,
  input  Input_Enable,
  input  Output_Enable,
  input  Clock,
  input  Clear,
  output [3:0] Output
);

  wire and_1_out;
  wire [3:0] register_1_q;

  Register #(.width(4)) register_1 (.D(Data), .en(and_1_out), .Q(register_1_q), .clk(and_1_out), .clr(Clear));
  and and_1 (and_1_out, Input_Enable, ~Clock);  // AND_Gate
  assign Output = Output_Enable ? register_1_q : 4'bz;  // Controlled_Buffer controlled_buffer_1

  // Notes on the sheet:
  //   General purpose 4bit register
endmodule
